# Fritzing sketch EEZYbotARM_PCA9685_v1 (saved by Fritzing 0.9.4)
breadboards: 1

parts:
  Part1 = Arduino Uno (Rev3)
  PCA9685 = PCA9685 16x12-bit PWM Breakout
  Main_arm_(q2) = Basic Servo
  EzzyBotArm_base_(q1) = Basic Servo
  Horarm_(q3) = Basic Servo
  J1 = Dagu DGServo 9g header connector (female) [package=THT]
  J2 = Dagu DGServo 9g header connector (female) [package=THT]
  J3 = Dagu DGServo 9g header connector (female) [package=THT]
  J4 = Dagu DGServo 9g header connector (female) [package=THT]
  End_Effector_(EE) = Basic Servo
  Battery_Pack_<_6_volts = 4 x AAA Battery Mount
  Buzzer_or_Piezo_Speaker = Piezo Speaker
  Resistor_(used_to_adjust_volume) = Resistor [tolerance=±5% resistance=100 package="2010 [SMD]"]

nets:
  N1: Part1.A4/SDA, PCA9685.no_name_yet#504
  N2: Part1.A5/SCL, PCA9685.no_name_yet#503
  N3: Part1.GND, PCA9685.no_name_yet#501, PCA9685.no_name_yet#701, PCA9685.no_name_yet#1000, PCA9685.no_name_yet#1001, PCA9685.no_name_yet#1002, PCA9685.no_name_yet#1003, Battery_Pack_<_6_volts.-, Resistor_(used_to_adjust_volume).Pin_0
  N4: Part1.D5_PWM, Buzzer_or_Piezo_Speaker.pin2
  N5: Part1.5V, PCA9685.no_name_yet#505
  N6: PCA9685.no_name_yet#0, J1.gnd, End_Effector_(EE).pulse
  N7: PCA9685.no_name_yet#1, EzzyBotArm_base_(q1).pulse, J2.gnd
  N8: PCA9685.no_name_yet#2, Main_arm_(q2).pulse, J3.gnd
  N9: PCA9685.no_name_yet#3, Horarm_(q3).pulse, J4.gnd
  N10: PCA9685.no_name_yet#100, PCA9685.no_name_yet#101, PCA9685.no_name_yet#102, PCA9685.no_name_yet#103, PCA9685.no_name_yet#706, Battery_Pack_<_6_volts.+
  N11: Buzzer_or_Piezo_Speaker.pin1, Resistor_(used_to_adjust_volume).Pin_1

notes:
  --- Schematic for the easyEAZYbotARM setup ---
  --Note--
  - Servo motors are labelled according to EEZYbotARM CAD files
  - Buzzer is optional (but useful for debugging)
  drawing v1, 15th May 2020
